// Logisim project Lab1 Circuit Diagram.circ as structural Verilog: 1 circuit, main circuit main
module main (
  input  A,
  input  B,
  input  C,
  output out_4
);

  wire and_1_out, and_2_out, and_3_out, not_1_out, not_2_out;

  not not_1 (not_1_out, A);
  not not_2 (not_2_out, B);
  and and_1 (and_1_out, not_1_out, C);
  and and_2 (and_2_out, not_2_out, A);
  and and_3 (and_3_out, B, C);
  or or_1 (out_4, and_1_out, and_2_out, and_3_out);
endmodule
