// Logisim project Lab1 IC Diagram.circ as structural Verilog: 4 circuits, main circuit main
module main (
  input  A,
  input  B,
  input  C,
  output out_4
);

  wire n7404_not_1_out_7, n7404_not_1_out_10, n7408_and_1_out_9, n7408_and_1_out_11, n7408_and_1_out_12,
       n7432_or_1_out_9;

  _7404_NOT u_7404_not_1 (
    .in_1(A), .in_4(B), .out_7(n7404_not_1_out_7), .out_10(n7404_not_1_out_10));  // open: in_2, in_3, in_5, in_6, out_8, out_9, out_11, out_12
  _7432_OR u_7432_or_1 (
    .in_1(n7408_and_1_out_11), .in_2(n7408_and_1_out_9), .in_3(n7432_or_1_out_9), .in_4(n7408_and_1_out_12),
    .out_9(n7432_or_1_out_9), .out_10(out_4));  // open: in_5, in_6, in_7, in_8, out_11, out_12
  _7408_AND u_7408_and_1 (
    .in_1(A), .in_2(n7404_not_1_out_10), .in_5(n7404_not_1_out_7), .in_6(C), .in_7(B), .in_8(C),
    .out_9(n7408_and_1_out_9), .out_11(n7408_and_1_out_11), .out_12(n7408_and_1_out_12));  // open: in_3, in_4, out_10

  // Notes on the sheet:
  //   A'
endmodule

module _7408_AND (
  input  in_1,
  input  in_2,
  input  in_3,
  input  in_4,
  input  in_5,
  input  in_6,
  input  in_7,
  input  in_8,
  output out_9,
  output out_10,
  output out_11,
  output out_12
);

  and and_1 (out_9, in_1, in_2);
  and and_2 (out_10, in_3, in_4);
  and and_3 (out_11, in_5, in_6);
  and and_4 (out_12, in_7, in_8);
endmodule

module _7432_OR (
  input  in_1,
  input  in_2,
  input  in_3,
  input  in_4,
  input  in_5,
  input  in_6,
  input  in_7,
  input  in_8,
  output out_9,
  output out_10,
  output out_11,
  output out_12
);

  or or_1 (out_9, in_1, in_2);
  or or_2 (out_10, in_3, in_4);
  or or_3 (out_11, in_5, in_6);
  or or_4 (out_12, in_7, in_8);
endmodule

module _7404_NOT (
  input  in_1,
  input  in_2,
  input  in_3,
  input  in_4,
  input  in_5,
  input  in_6,
  output out_7,
  output out_8,
  output out_9,
  output out_10,
  output out_11,
  output out_12
);

  not not_1 (out_7, in_1);
  not not_2 (out_8, in_2);
  not not_3 (out_9, in_3);
  not not_4 (out_10, in_4);
  not not_5 (out_11, in_5);
  not not_6 (out_12, in_6);
endmodule
