// Logisim project AND by NAND.circ as structural Verilog: 1 circuit, main circuit main
module main (
  input  A,
  input  B,
  output out_3
);

  wire nand_1_out;

  nand nand_1 (nand_1_out, A, B);
  nand nand_2 (out_3, nand_1_out, nand_1_out);
endmodule
