// Logisim project LAB2 Circuit Diagram (NAND).circ as structural Verilog: 1 circuit, main circuit main
module main (
  input  A,
  input  B,
  input  C,
  output out_4
);

  wire nand_1_out, nand_2_out, nand_3_out, nand_4_out, nand_5_out, nand_6_out, nand_7_out;

  nand nand_1 (nand_1_out, A, C);
  nand nand_2 (nand_2_out, C, C);
  nand nand_3 (nand_3_out, B, nand_2_out);
  nand nand_4 (nand_4_out, nand_1_out, nand_1_out);
  nand nand_5 (nand_5_out, nand_3_out, nand_3_out);
  nand nand_6 (nand_6_out, nand_4_out, nand_4_out);
  nand nand_7 (nand_7_out, nand_5_out, nand_5_out);
  nand nand_8 (out_4, nand_6_out, nand_7_out);
endmodule
