// Logisim project NAND IC 7400.circ as structural Verilog: 1 circuit, main circuit main
module main (
  input  A,
  input  B,
  input  A_2,
  input  B_2,
  input  A_3,
  input  B_3,
  input  A_4,
  input  B_4,
  output out_9,
  output out_10,
  output out_11,
  output out_12
);

  nand nand_1 (out_9, A, B);
  nand nand_2 (out_10, A_2, B_2);
  nand nand_3 (out_11, A_3, B_3);
  nand nand_4 (out_12, A_4, B_4);
endmodule
