// Logisim project NOR IC 7402.circ as structural Verilog: 1 circuit, main circuit main
module main (
  input  A,
  input  B,
  input  A_2,
  input  B_2,
  input  A_3,
  input  B_3,
  input  A_4,
  input  B_4,
  output out_9,
  output out_10,
  output out_11,
  output out_12
);

  nor nor_1 (out_9, A, B);
  nor nor_2 (out_10, A_2, B_2);
  nor nor_3 (out_11, A_3, B_3);
  nor nor_4 (out_12, A_4, B_4);
endmodule
