// Logisim project LAB 3 - 1st Canonical Form.circ as structural Verilog: 1 circuit, main circuit main
module main (
  input  A,
  input  B,
  input  C,
  output out_4
);

  wire main_1_out_10, main_1_out_11, main_1_out_12, main_2_out_10, main_2_out_11, main_2_out_12;

  Not_Gate_IC_7404_main main_1 (
    .in_4(A), .in_5(B), .in_6(C), .out_10(main_1_out_10), .out_11(main_1_out_11), .out_12(main_1_out_12));  // open: in_1, in_2, in_3, out_7, out_8, out_9
  _3_input_And_gate_7411_main main_2 (
    .in_1(main_1_out_10), .in_2(main_1_out_11), .in_3(C), .in_4(A), .in_5(B), .in_6(main_1_out_12),
    .in_7(main_1_out_10), .in_8(B), .in_9(main_1_out_12), .out_10(main_2_out_10), .out_11(main_2_out_11),
    .out_12(main_2_out_12));
  _3_input_OR_gate_4075_main main_3 (
    .in_4(main_2_out_10), .in_5(main_2_out_11), .in_6(main_2_out_12), .out_11(out_4));  // open: in_1, in_2, in_3, in_7, in_8, in_9, out_10, out_12

  // Notes on the sheet:
  //   A'
  //   B'
endmodule
