// Logisim project LAB 3 - 2nd Canonical Form.circ as structural Verilog: 1 circuit, main circuit main
module main (
  input  A,
  input  B,
  input  C,
  output out_4
);

  wire main_1_out_10, main_1_out_11, main_1_out_12, main_2_out_10, main_2_out_11, main_2_out_12,
       main_3_out_11, main_3_out_12, main_4_out_10;

  Not_Gate_IC_7404_main main_1 (
    .in_4(A), .in_5(B), .in_6(C), .out_10(main_1_out_10), .out_11(main_1_out_11), .out_12(main_1_out_12));  // open: in_1, in_2, in_3, out_7, out_8, out_9
  _3_input_OR_gate_4075_main main_2 (
    .in_1(A), .in_2(main_1_out_11), .in_3(main_1_out_12), .in_4(main_1_out_10), .in_5(B), .in_6(C), .in_7(A),
    .in_8(B), .in_9(C), .out_10(main_2_out_10), .out_11(main_2_out_11), .out_12(main_2_out_12));
  _3_input_OR_gate_4075_main main_3 (
    .in_4(main_1_out_10), .in_5(main_1_out_11), .in_6(main_1_out_12), .in_7(main_1_out_10), .in_8(B),
    .in_9(main_1_out_12), .out_11(main_3_out_11), .out_12(main_3_out_12));  // open: in_1, in_2, in_3, out_10
  _3_input_And_gate_7411_main main_4 (
    .in_1(main_2_out_12), .in_2(main_2_out_10), .in_3(main_2_out_11), .in_7(main_4_out_10),
    .in_8(main_3_out_12), .in_9(main_3_out_11), .out_10(main_4_out_10), .out_12(out_4));  // open: in_4, in_5, in_6, out_11
endmodule
