// Logisim project Lab 4 - BCD to Excess-3.circ as structural Verilog: 4 circuits, main circuit main
module main (
  input  W,
  input  X,
  input  Y,
  input  Z,
  output A,
  output B,
  output C,
  output D
);

  wire and_ic_7408_1_out_9, and_ic_7408_1_out_10, and_ic_7408_1_out_11, and_ic_7408_1_out_12,
       and_ic_7408_2_out_9, and_ic_7408_2_out_10, and_ic_7408_2_out_11, and_ic_7408_2_out_12,
       not_ic_7404_1_out_10, not_ic_7404_1_out_11, or_ic_7432_1_out_10, or_ic_7432_1_out_12;

  AND_IC_7408 and_ic_7408_1 (
    .in_1(not_ic_7404_1_out_10), .in_2(Y), .in_3(not_ic_7404_1_out_10), .in_4(Z), .in_5(X), .in_6(Y),
    .in_7(X), .in_8(Z), .out_9(and_ic_7408_1_out_9), .out_10(and_ic_7408_1_out_10),
    .out_11(and_ic_7408_1_out_11), .out_12(and_ic_7408_1_out_12));
  NOT_IC_7404 not_ic_7404_1 (
    .in_4(X), .in_5(Y), .in_6(Z), .out_10(not_ic_7404_1_out_10), .out_11(not_ic_7404_1_out_11), .out_12(D));  // open: in_1, in_2, in_3, out_7, out_8, out_9
  OR_IC_7432 or_ic_7432_1 (
    .in_1(and_ic_7408_2_out_12), .in_2(or_ic_7432_1_out_10), .in_3(and_ic_7408_1_out_10),
    .in_4(and_ic_7408_1_out_9), .in_5(W), .in_6(or_ic_7432_1_out_12), .in_7(and_ic_7408_1_out_12),
    .in_8(and_ic_7408_1_out_11), .out_9(B), .out_10(or_ic_7432_1_out_10), .out_11(A),
    .out_12(or_ic_7432_1_out_12));
  AND_IC_7408 and_ic_7408_2 (
    .in_1(Y), .in_2(Z), .in_3(not_ic_7404_1_out_11), .in_4(D), .in_5(X), .in_6(not_ic_7404_1_out_11),
    .in_7(and_ic_7408_2_out_11), .in_8(D), .out_9(and_ic_7408_2_out_9), .out_10(and_ic_7408_2_out_10),
    .out_11(and_ic_7408_2_out_11), .out_12(and_ic_7408_2_out_12));
  OR_IC_7432 or_ic_7432_2 (
    .in_7(and_ic_7408_2_out_10), .in_8(and_ic_7408_2_out_9), .out_12(C));  // open: in_1, in_2, in_3, in_4, in_5, in_6, out_9, out_10, out_11

  // Notes on the sheet:
  //   B'
  //   C'
  //   D'
endmodule

module AND_IC_7408 (
  input  in_1,
  input  in_2,
  input  in_3,
  input  in_4,
  input  in_5,
  input  in_6,
  input  in_7,
  input  in_8,
  output out_9,
  output out_10,
  output out_11,
  output out_12
);

  and and_1 (out_9, in_1, in_2);
  and and_2 (out_10, in_3, in_4);
  and and_3 (out_11, in_5, in_6);
  and and_4 (out_12, in_7, in_8);
endmodule

module NOT_IC_7404 (
  input  in_1,
  input  in_2,
  input  in_3,
  input  in_4,
  input  in_5,
  input  in_6,
  output out_7,
  output out_8,
  output out_9,
  output out_10,
  output out_11,
  output out_12
);

  not not_1 (out_7, in_1);
  not not_2 (out_8, in_2);
  not not_3 (out_9, in_3);
  not not_4 (out_10, in_4);
  not not_5 (out_11, in_5);
  not not_6 (out_12, in_6);
endmodule

module OR_IC_7432 (
  input  in_1,
  input  in_2,
  input  in_3,
  input  in_4,
  input  in_5,
  input  in_6,
  input  in_7,
  input  in_8,
  output out_9,
  output out_10,
  output out_11,
  output out_12
);

  or or_1 (out_9, in_1, in_2);
  or or_2 (out_10, in_3, in_4);
  or or_3 (out_11, in_5, in_6);
  or or_4 (out_12, in_7, in_8);
endmodule
